// Logisim project random.circ as structural Verilog: 1 circuit, main circuit main
module main (
);

  wire and_1_out, clock_1_out, or_1_out;
  wire [15:0] counter_1_q;

  and and_1 (and_1_out, or_1_out, clock_1_out);
  Clock clock_1 (.out(clock_1_out));
  Counter #(.width(16), .max('hffff)) counter_1 (
    .load(1'b1), .count(1'b1), .Q(counter_1_q), .clk(and_1_out));  // open: D, carry, clr
  Random #(.width(16), .seed(4040)) random_1 (.clk(and_1_out));  // open: next, out, clr
  or or_1 (or_1_out, counter_1_q[15], counter_1_q[14], counter_1_q[13], counter_1_q[12], counter_1_q[11], counter_1_q[10], counter_1_q[9], counter_1_q[8], counter_1_q[6], counter_1_q[5], counter_1_q[4], counter_1_q[3], counter_1_q[2], counter_1_q[1], counter_1_q[0], counter_1_q[7]);
endmodule
